# Fritzing sketch CarpelSense Fritz (FIN) (saved by Fritzing 1.0.6)
breadboards: 1

parts:
  BATT1 = FKIT-COIN_CELL [package=fkit-lir2450-h]
  A1 = MYOWARE Muscle sensor
  Short_Flex_Sensor = Basic Flex Resistor
  R8 = Resistor [tolerance=±10% resistance=4.7k package="0603 [SMD]"]
  M3 = Arduino Nano 33 IOT-tht

nets:
  N1: BATT1.NEG, A1.Pin_5, R8.Pin_1, M3.pin_5, M3.pin_14, M3.pin_19
  N2: BATT1.POS, M3.pin_15
  N3: A1.Pin_4, Short_Flex_Sensor.Pin_2, M3.pin_2, M3.pin_7, M3.pin_9
  N4: A1.Pin_6, M3.pin_4
  N5: Short_Flex_Sensor.pin_1, R8.Pin_0, M3.pin_10
  N6: M3.pin_13, M3.pin_18

custom parts:
  MYOWARE Muscle sensor: The MyoWare® 2.0 Muscle Sensor is an Arduino-compatible, all-in-one electromyography (EMG) sensor from Advancer Technologies.
  Arduino Nano 33 IOT-tht: The Arduino Nano 33 IoT is the easiest and cheapest point of entry to enhance existing devices (and creating new ones) to be part of the IoT and designing pico-network applications. Whether you are looking at building a sensor network connected to your office or home router, or if you want to create a BLE device sending data to a cellphone, the Nano 33 IoT is your one-stop-solution for many of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
