# Fritzing sketch CarpelSense Fritz (saved by Fritzing 1.0.6)
breadboards: 1

parts:
  BATT1 = FKIT-COIN_CELL [package=fkit-lir2450-h]
  R4 = Resistor [tolerance=±10% resistance=4.7k package="0603 [SMD]"]
  A1 = MYOWARE Muscle sensor
  A2 = Pololu U3V40F12
  Short_Flex_Sensor = Basic Flex Resistor
  M2 = Arduino Nano 33 IOT-tht

nets:
  N1: BATT1.NEG, A2.Pin_4, A2.Pin_5
  N2: BATT1.POS, A2.Pin_2
  N3: R4.Pin_0, A1.Pin_5, M2.pin_14, M2.pin_19
  N4: R4.Pin_1, Short_Flex_Sensor.pin_1, M2.pin_8, M2.pin_9
  N5: A1.Pin_4, Short_Flex_Sensor.Pin_2, M2.pin_2
  N6: A1.Pin_6, M2.pin_4
  N7: A2.Pin_6, M2.pin_15
  N8: M2.pin_13, M2.pin_18

custom parts:
  MYOWARE Muscle sensor: The MyoWare® 2.0 Muscle Sensor is an Arduino-compatible, all-in-one electromyography (EMG) sensor from Advancer Technologies.
  Pololu U3V40F12: This compact (0.6″×0.6″) switching step-up (or boost) voltage regulator efficiently generates 12 V from input voltages as low as 1.3 V and handles continuous input currents up to 3.5 A.
  Arduino Nano 33 IOT-tht: The Arduino Nano 33 IoT is the easiest and cheapest point of entry to enhance existing devices (and creating new ones) to be part of the IoT and designing pico-network applications. Whether you are looking at building a sensor network connected to your office or home router, or if you want to create a BLE device sending data to a cellphone, the Nano 33 IoT is your one-stop-solution for many of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
