# Fritzing sketch CarpelSense Fritz (FIN) (saved by Fritzing 1.0.6)
breadboards: 1

parts:
  Short_Flex_Sensor = Basic Flex Resistor
  R8 = Resistor [tolerance=±10% resistance=4.7k package="0603 [SMD]"]
  M3 = Arduino Nano 33 IOT-tht
  A1 = DFR SEN0240

nets:
  N1: Short_Flex_Sensor.Pin_2, M3.pin_2, A1.Pin_2
  N2: Short_Flex_Sensor.pin_1, R8.Pin_0, M3.pin_10
  N3: R8.Pin_1, M3.pin_14, M3.pin_19, A1.Pin_3
  N4: M3.pin_9, A1.Pin_1
  N5: M3.pin_13, M3.pin_18

custom parts:
  Arduino Nano 33 IOT-tht: The Arduino Nano 33 IoT is the easiest and cheapest point of entry to enhance existing devices (and creating new ones) to be part of the IoT and designing pico-network applications. Whether you are looking at building a sensor network connected to your office or home router, or if you want to create a BLE device sending data to a cellphone, the Nano 33 IoT is your one-stop-solution for many of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
  DFR SEN0240: This EMG sensor is launched by the cooperation of DFRobot and OYMotion, which can detect sEMG to reflect muscle and neural activities of human.
